// Digital circuit ALU.dig as structural Verilog
module ALU (
  input  [7:0] B,
  input  [7:0] A,
  input  Sub,
  output [7:0] S,
  output C,
  output Z
);

  wire A31, AND_1, AND_2, B31, B31_t, OR, S31;
  wire [6:0] B_t_t;
  wire [7:0] B_t;

  nor nor_1 (Z, A[0], A[1], A[2], A[3], A[4], A[5], A[6], A[7], B[0], B[1], B[2], B[3], B[4], B[5], B[6], B[7]);
  assign B_t = B ^ {8{1'b1}};  // XOr xor_1, 8 bits wide
  Multiplexer #(.Bits(8)) multiplexer_1 (.sel(Sub), .in_0(B), .in_1(B_t), .out({B31_t, B_t_t}));
  Add #(.Bits(8)) add_1 (.a(A), .b({B31_t, B_t_t}), .c_i(Sub), .s(S), .c_o(C));
  and u_and_1 (AND_1, A31, B31, S[7]);
  and u_and_2 (AND_2, A[7], B31_t, S31);
  not not_1 (A31, A[7]);
  not not_2 (B31, B31_t);
  not not_3 (S31, S[7]);
  or or_1 (OR, AND_1, AND_2);

  // Other names for the same wires on the sheet: A31_t = A[7]; B_t_t[7] = B31_t; C_o = C; SUM[7:0] = S; S31_t = S[7]
endmodule
