// Digital circuit ALU_git.dig as structural Verilog
module ALU_git (
  input  [7:0] B,
  input  [7:0] A,
  input  SUB,
  output C,
  output Z,
  output [7:0] S
);

  wire and_1_out, and_2_out, and_3_out, and_4_out, and_5_out, and_6_out, and_7_out, and_8_out, and_9_out,
       and_10_out, and_11_out, and_12_out, and_13_out, and_14_out, and_15_out, and_16_out, and_17_out,
       and_18_out, and_19_out, and_20_out, and_21_out, and_22_out, and_23_out, and_24_out, and_25_out,
       and_26_out, and_27_out, and_28_out, and_29_out, and_30_out, and_31_out, and_32_out, and_33_out,
       and_34_out, and_35_out, and_36_out, and_37_out, and_38_out, and_39_out, and_40_out, and_41_out,
       and_42_out, and_43_out, and_44_out, and_45_out, and_46_out, and_47_out, and_48_out, and_49_out,
       and_50_out, and_51_out, and_52_out, and_53_out, and_54_out, and_55_out, and_56_out, and_57_out,
       and_58_out, and_59_out, and_60_out, and_61_out, and_62_out, and_63_out, and_64_out, and_65_out,
       and_66_out, and_67_out, and_68_out, and_69_out, and_70_out, and_71_out, and_72_out, and_73_out,
       and_74_out, and_75_out, and_76_out, and_77_out, and_78_out, and_79_out, and_80_out, not_1_out,
       not_2_out, not_3_out, not_4_out, not_5_out, not_6_out, not_7_out, not_8_out, not_9_out, not_10_out,
       not_11_out, not_12_out, not_13_out, not_14_out, not_15_out, not_16_out, not_17_out, not_18_out,
       not_19_out, not_20_out, not_21_out, not_22_out, not_23_out, not_24_out, not_25_out, not_26_out,
       not_27_out, not_28_out, not_29_out, not_30_out, not_31_out, not_32_out, not_33_out, not_34_out,
       not_35_out, not_36_out, not_37_out, not_38_out, not_39_out, not_40_out, not_41_out, not_42_out,
       not_43_out, not_44_out, not_45_out, not_46_out, not_47_out, not_48_out, not_49_out, not_50_out,
       not_51_out, not_52_out, not_53_out, not_54_out, not_55_out, not_56_out, or_1_out, or_2_out, or_3_out,
       or_4_out, or_5_out, or_6_out, or_7_out, or_8_out, or_9_out, or_10_out, or_11_out, or_12_out,
       or_13_out, or_14_out, or_15_out, or_16_out, or_17_out, or_18_out, or_19_out, or_20_out, or_21_out,
       or_22_out, or_23_out, or_24_out, or_25_out, or_26_out, or_27_out, or_28_out, or_29_out, or_30_out,
       or_31_out;

  not not_1 (not_1_out, 1'b1);
  not not_2 (not_2_out, B[0]);
  not not_3 (not_3_out, 1'b1);
  not not_4 (not_4_out, B[1]);
  not not_5 (not_5_out, 1'b1);
  not not_6 (not_6_out, B[2]);
  not not_7 (not_7_out, 1'b1);
  not not_8 (not_8_out, B[3]);
  not not_9 (not_9_out, 1'b1);
  not not_10 (not_10_out, B[4]);
  not not_11 (not_11_out, 1'b1);
  not not_12 (not_12_out, B[5]);
  not not_13 (not_13_out, 1'b1);
  not not_14 (not_14_out, B[6]);
  not not_15 (not_15_out, 1'b1);
  not not_16 (not_16_out, B[7]);
  and and_1 (and_1_out, B[0], not_1_out);
  and and_2 (and_2_out, not_2_out, 1'b1);
  and and_3 (and_3_out, B[1], not_3_out);
  and and_4 (and_4_out, not_4_out, 1'b1);
  and and_5 (and_5_out, B[2], not_5_out);
  and and_6 (and_6_out, not_6_out, 1'b1);
  and and_7 (and_7_out, B[3], not_7_out);
  and and_8 (and_8_out, not_8_out, 1'b1);
  and and_9 (and_9_out, B[4], not_9_out);
  and and_10 (and_10_out, not_10_out, 1'b1);
  and and_11 (and_11_out, B[5], not_11_out);
  and and_12 (and_12_out, not_12_out, 1'b1);
  and and_13 (and_13_out, B[6], not_13_out);
  and and_14 (and_14_out, not_14_out, 1'b1);
  and and_15 (and_15_out, B[7], not_15_out);
  and and_16 (and_16_out, not_16_out, 1'b1);
  or or_1 (or_1_out, and_1_out, and_2_out);
  or or_2 (or_2_out, and_3_out, and_4_out);
  or or_3 (or_3_out, and_5_out, and_6_out);
  or or_4 (or_4_out, and_7_out, and_8_out);
  or or_5 (or_5_out, and_9_out, and_10_out);
  or or_6 (or_6_out, and_11_out, and_12_out);
  or or_7 (or_7_out, and_13_out, and_14_out);
  or or_8 (or_8_out, and_15_out, and_16_out);
  and and_17 (and_17_out, SUB, or_1_out);
  not not_17 (not_17_out, SUB);
  and and_18 (and_18_out, not_17_out, B[0]);
  and and_19 (and_19_out, SUB, or_2_out);
  not not_18 (not_18_out, SUB);
  and and_20 (and_20_out, not_18_out, B[1]);
  and and_21 (and_21_out, SUB, or_3_out);
  not not_19 (not_19_out, SUB);
  and and_22 (and_22_out, not_19_out, B[2]);
  and and_23 (and_23_out, SUB, or_4_out);
  not not_20 (not_20_out, SUB);
  and and_24 (and_24_out, not_20_out, B[3]);
  and and_25 (and_25_out, SUB, or_5_out);
  not not_21 (not_21_out, SUB);
  and and_26 (and_26_out, not_21_out, B[4]);
  and and_27 (and_27_out, SUB, or_6_out);
  not not_22 (not_22_out, SUB);
  and and_28 (and_28_out, not_22_out, B[5]);
  and and_29 (and_29_out, SUB, or_7_out);
  not not_23 (not_23_out, SUB);
  and and_30 (and_30_out, not_23_out, B[6]);
  and and_31 (and_31_out, SUB, or_8_out);
  not not_24 (not_24_out, SUB);
  and and_32 (and_32_out, not_24_out, B[7]);
  or or_9 (or_9_out, and_17_out, and_18_out);
  or or_10 (or_10_out, and_19_out, and_20_out);
  or or_11 (or_11_out, and_21_out, and_22_out);
  or or_12 (or_12_out, and_23_out, and_24_out);
  or or_13 (or_13_out, and_25_out, and_26_out);
  or or_14 (or_14_out, and_27_out, and_28_out);
  or or_15 (or_15_out, and_29_out, and_30_out);
  or or_16 (or_16_out, and_31_out, and_32_out);
  and and_33 (and_33_out, A[0], not_25_out);
  not not_25 (not_25_out, or_9_out);
  not not_26 (not_26_out, A[0]);
  and and_34 (and_34_out, not_26_out, or_9_out);
  and and_35 (and_35_out, or_9_out, A[0]);
  and and_36 (and_36_out, A[1], not_27_out);
  not not_27 (not_27_out, or_10_out);
  not not_28 (not_28_out, A[1]);
  and and_37 (and_37_out, not_28_out, or_10_out);
  and and_38 (and_38_out, or_10_out, A[1]);
  and and_39 (and_39_out, A[2], not_29_out);
  not not_29 (not_29_out, or_11_out);
  not not_30 (not_30_out, A[2]);
  and and_40 (and_40_out, not_30_out, or_11_out);
  and and_41 (and_41_out, or_11_out, A[2]);
  and and_42 (and_42_out, A[3], not_31_out);
  not not_31 (not_31_out, or_12_out);
  not not_32 (not_32_out, A[3]);
  and and_43 (and_43_out, not_32_out, or_12_out);
  and and_44 (and_44_out, or_12_out, A[3]);
  and and_45 (and_45_out, A[4], not_33_out);
  not not_33 (not_33_out, or_13_out);
  not not_34 (not_34_out, A[4]);
  and and_46 (and_46_out, not_34_out, or_13_out);
  and and_47 (and_47_out, or_13_out, A[4]);
  and and_48 (and_48_out, A[5], not_35_out);
  not not_35 (not_35_out, or_14_out);
  not not_36 (not_36_out, A[5]);
  and and_49 (and_49_out, not_36_out, or_14_out);
  and and_50 (and_50_out, or_14_out, A[5]);
  and and_51 (and_51_out, A[6], not_37_out);
  not not_37 (not_37_out, or_15_out);
  not not_38 (not_38_out, A[6]);
  and and_52 (and_52_out, not_38_out, or_15_out);
  and and_53 (and_53_out, or_15_out, A[6]);
  and and_54 (and_54_out, A[7], not_39_out);
  not not_39 (not_39_out, or_16_out);
  not not_40 (not_40_out, A[7]);
  and and_55 (and_55_out, not_40_out, or_16_out);
  and and_56 (and_56_out, or_16_out, A[7]);
  or or_17 (or_17_out, and_33_out, and_34_out);
  or or_18 (or_18_out, and_59_out, and_35_out);
  or or_19 (or_19_out, and_36_out, and_37_out);
  or or_20 (or_20_out, and_62_out, and_38_out);
  or or_21 (or_21_out, and_39_out, and_40_out);
  or or_22 (or_22_out, and_65_out, and_41_out);
  or or_23 (or_23_out, and_42_out, and_43_out);
  or or_24 (or_24_out, and_68_out, and_44_out);
  or or_25 (or_25_out, and_45_out, and_46_out);
  or or_26 (or_26_out, and_71_out, and_47_out);
  or or_27 (or_27_out, and_48_out, and_49_out);
  or or_28 (or_28_out, and_74_out, and_50_out);
  or or_29 (or_29_out, and_51_out, and_52_out);
  or or_30 (or_30_out, and_77_out, and_53_out);
  or or_31 (or_31_out, and_54_out, and_55_out);
  // Or or_32 has open pins: In_1=and_80_out, In_2=and_56_out, out=open
  and and_57 (and_57_out, SUB, not_41_out);
  not not_41 (not_41_out, or_17_out);
  and and_58 (and_58_out, not_42_out, or_17_out);
  not not_42 (not_42_out, SUB);
  and and_59 (and_59_out, SUB, or_17_out);
  and and_60 (and_60_out, or_18_out, not_43_out);
  not not_43 (not_43_out, or_19_out);
  and and_61 (and_61_out, not_44_out, or_19_out);
  not not_44 (not_44_out, or_18_out);
  and and_62 (and_62_out, or_18_out, or_19_out);
  and and_63 (and_63_out, or_20_out, not_45_out);
  not not_45 (not_45_out, or_21_out);
  and and_64 (and_64_out, not_46_out, or_21_out);
  not not_46 (not_46_out, or_20_out);
  and and_65 (and_65_out, or_20_out, or_21_out);
  and and_66 (and_66_out, or_22_out, not_47_out);
  not not_47 (not_47_out, or_23_out);
  and and_67 (and_67_out, not_48_out, or_23_out);
  not not_48 (not_48_out, or_22_out);
  and and_68 (and_68_out, or_22_out, or_23_out);
  and and_69 (and_69_out, or_24_out, not_49_out);
  not not_49 (not_49_out, or_25_out);
  and and_70 (and_70_out, not_50_out, or_25_out);
  not not_50 (not_50_out, or_24_out);
  and and_71 (and_71_out, or_24_out, or_25_out);
  and and_72 (and_72_out, or_26_out, not_51_out);
  not not_51 (not_51_out, or_27_out);
  and and_73 (and_73_out, not_52_out, or_27_out);
  not not_52 (not_52_out, or_26_out);
  and and_74 (and_74_out, or_26_out, or_27_out);
  and and_75 (and_75_out, or_28_out, not_53_out);
  not not_53 (not_53_out, or_29_out);
  and and_76 (and_76_out, not_54_out, or_29_out);
  not not_54 (not_54_out, or_28_out);
  and and_77 (and_77_out, or_28_out, or_29_out);
  and and_78 (and_78_out, or_30_out, not_55_out);
  not not_55 (not_55_out, or_31_out);
  and and_79 (and_79_out, not_56_out, or_31_out);
  not not_56 (not_56_out, or_30_out);
  and and_80 (and_80_out, or_30_out, or_31_out);
  or or_33 (S[0], and_57_out, and_58_out);
  or or_34 (S[1], and_60_out, and_61_out);
  or or_35 (S[2], and_63_out, and_64_out);
  or or_36 (S[3], and_66_out, and_67_out);
  or or_37 (S[4], and_69_out, and_70_out);
  or or_38 (S[5], and_72_out, and_73_out);
  or or_39 (S[6], and_75_out, and_76_out);
  or or_40 (C, and_78_out, and_79_out);
  nor nor_1 (Z, S[0], S[1], S[2], S[3], S[4], S[5], S[6], C);

  assign S[7] = C;
endmodule
