// Digital circuit CC.dig as structural Verilog
module CC (
  input  en,
  input  CLK,
  output C0,
  output C1,
  output C2
);

  wire and_1_out, and_2_out, and_3_out, and_4_out, and_5_out, and_6_out, and_7_out, and_8_out, and_9_out,
       and_10_out, and_11_out, and_12_out, and_13_out, and_14_out, and_15_out, and_16_out, nC2, not_1_out,
       not_2_out, not_3_out, not_4_out, not_5_out, not_6_out, not_7_out, not_8_out, not_9_out, or_1_out,
       or_2_out, or_3_out, or_4_out, or_5_out, or_6_out, or_7_out, or_8_out;

  and and_1 (and_1_out, C0, C1);
  or or_1 (or_1_out, C0, nC2);
  or or_2 (or_2_out, and_1_out, C2);
  and and_2 (and_2_out, en, or_1_out);
  and and_3 (and_3_out, en, C0);
  and and_4 (and_4_out, en, or_2_out);
  not not_1 (not_1_out, and_2_out);
  not not_2 (not_2_out, C0);
  not not_3 (not_3_out, and_3_out);
  not not_4 (not_4_out, C1);
  not not_5 (not_5_out, and_4_out);
  not not_6 (not_6_out, C2);
  and and_5 (and_5_out, not_1_out, C0);
  and and_6 (and_6_out, and_2_out, not_2_out);
  and and_7 (and_7_out, not_3_out, C1);
  and and_8 (and_8_out, and_3_out, not_4_out);
  and and_9 (and_9_out, not_5_out, C2);
  and and_10 (and_10_out, and_4_out, not_6_out);
  or or_3 (or_3_out, and_5_out, and_6_out);
  or or_4 (or_4_out, and_7_out, and_8_out);
  or or_5 (or_5_out, and_9_out, and_10_out);
  and and_11 (and_11_out, or_6_out, CLK);
  and and_12 (and_12_out, or_3_out, not_7_out);
  not not_7 (not_7_out, CLK);
  and and_13 (and_13_out, or_7_out, CLK);
  and and_14 (and_14_out, or_4_out, not_8_out);
  not not_8 (not_8_out, CLK);
  and and_15 (and_15_out, or_8_out, CLK);
  and and_16 (and_16_out, or_5_out, not_9_out);
  not not_9 (not_9_out, CLK);
  or or_6 (or_6_out, and_11_out, and_12_out);
  or or_7 (or_7_out, and_13_out, and_14_out);
  or or_8 (or_8_out, and_15_out, and_16_out);
  Multiplexer multiplexer_1 (.sel(CLK), .in_0(C0), .in_1(or_6_out), .out(C0));
  Multiplexer multiplexer_2 (.sel(CLK), .in_0(C1), .in_1(or_7_out), .out(C1));
  Multiplexer multiplexer_3 (.sel(CLK), .in_0(C2), .in_1(or_8_out), .out(C2));
  not not_10 (nC2, C2);
endmodule
