// Digital circuit FLAG_git.dig as structural Verilog
module FLAG_git (
  input  CLK,
  input  en,
  input  Z,
  input  C,
  output Z_2,
  output C_2
);

  wire and_1_out, and_2_out, and_3_out, and_4_out, and_5_out, and_6_out, and_7_out, multiplexer_1_out,
       multiplexer_2_out, not_1_out, not_2_out, or_1_out, or_2_out;

  and and_1 (and_1_out, 1'b0, 1'b0);
  and and_2 (and_2_out, 1'b0, 1'b0);
  and and_3 (and_3_out, CLK, en);
  D_FF d_ff_1 (.D(Z), .C(and_3_out), .Q(Z_2));  // open: nQ
  D_FF d_ff_2 (.D(C), .C(and_3_out), .Q(C_2));  // open: nQ
  and and_4 (and_4_out, or_1_out, 1'b0);
  and and_5 (and_5_out, and_1_out, not_1_out);
  not not_1 (not_1_out, 1'b0);
  and and_6 (and_6_out, or_2_out, 1'b0);
  and and_7 (and_7_out, and_2_out, not_2_out);
  not not_2 (not_2_out, 1'b0);
  or or_1 (or_1_out, and_4_out, and_5_out);
  or or_2 (or_2_out, and_6_out, and_7_out);
  Multiplexer multiplexer_1 (.sel(1'b0), .in_0(multiplexer_1_out), .in_1(or_1_out), .out(multiplexer_1_out));
  Multiplexer multiplexer_2 (.sel(1'b0), .in_0(multiplexer_2_out), .in_1(or_2_out), .out(multiplexer_2_out));
endmodule
