// Digital circuit MAR.dig as structural Verilog
module MAR (
  input  [7:0] M,
  input  CLK,
  input  M_in,
  output [3:0] M_2
);

  wire and_1_out, and_2_out, and_3_out, and_4_out, and_5_out, and_6_out, and_7_out, and_8_out, and_9_out,
       and_10_out, multiplexer_1_out, multiplexer_2_out, multiplexer_3_out, multiplexer_4_out, not_1_out,
       not_2_out, not_3_out, not_4_out, or_1_out, or_2_out, or_3_out, or_4_out;

  and and_1 (and_1_out, 1'b1, 1'b0);
  not not_1 (not_1_out, and_1_out);
  not not_2 (not_2_out, and_1_out);
  not not_3 (not_3_out, and_1_out);
  not not_4 (not_4_out, and_1_out);
  and and_2 (and_2_out, or_1_out, and_1_out);
  and and_3 (and_3_out, 1'b0, not_1_out);
  and and_4 (and_4_out, or_2_out, and_1_out);
  and and_5 (and_5_out, 1'b0, not_2_out);
  and and_6 (and_6_out, or_3_out, and_1_out);
  and and_7 (and_7_out, 1'b0, not_3_out);
  and and_8 (and_8_out, or_4_out, and_1_out);
  and and_9 (and_9_out, 1'b0, not_4_out);
  or or_1 (or_1_out, and_2_out, and_3_out);
  or or_2 (or_2_out, and_4_out, and_5_out);
  or or_3 (or_3_out, and_6_out, and_7_out);
  or or_4 (or_4_out, and_8_out, and_9_out);
  Multiplexer multiplexer_1 (.sel(and_1_out), .in_0(multiplexer_1_out), .in_1(or_1_out), .out(multiplexer_1_out));
  Multiplexer multiplexer_2 (.sel(and_1_out), .in_0(multiplexer_2_out), .in_1(or_2_out), .out(multiplexer_2_out));
  Multiplexer multiplexer_3 (.sel(and_1_out), .in_0(multiplexer_3_out), .in_1(or_3_out), .out(multiplexer_3_out));
  Multiplexer multiplexer_4 (.sel(and_1_out), .in_0(multiplexer_4_out), .in_1(or_4_out), .out(multiplexer_4_out));
  and and_10 (and_10_out, CLK, M_in);
  D_FF d_ff_1 (.D(M[0]), .C(and_10_out), .Q(M_2[0]));  // open: nQ
  D_FF d_ff_2 (.D(M[1]), .C(and_10_out), .Q(M_2[1]));  // open: nQ
  D_FF d_ff_3 (.D(M[2]), .C(and_10_out), .Q(M_2[2]));  // open: nQ
  D_FF d_ff_4 (.D(M[3]), .C(and_10_out), .Q(M_2[3]));  // open: nQ
endmodule
