// Digital circuit PC.dig as structural Verilog
module PC (
  input  en,
  input  CLK,
  input  P_out,
  output [7:0] P
);

  wire and_1_out, and_2_out, and_3_out, and_4_out, and_5_out, and_6_out, and_7_out, and_8_out, and_9_out,
       and_10_out, and_11_out, and_12_out, and_13_out, and_14_out, and_15_out, and_16_out, and_17_out,
       and_18_out, and_19_out, not_1_out, not_2_out, not_3_out, not_4_out, not_5_out, not_6_out, not_7_out,
       not_8_out, not_9_out, not_10_out, not_11_out, not_12_out, or_1_out, or_2_out, or_3_out, or_4_out,
       or_5_out, or_6_out, or_7_out, or_8_out, P0, P1, P2, P3;

  and and_1 (and_1_out, en, P0);
  and and_2 (and_2_out, en, P0, P1);
  and and_3 (and_3_out, en, P0, P1, P2);
  not not_1 (not_1_out, en);
  not not_2 (not_2_out, P0);
  not not_3 (not_3_out, and_1_out);
  not not_4 (not_4_out, P1);
  not not_5 (not_5_out, and_2_out);
  not not_6 (not_6_out, P2);
  not not_7 (not_7_out, and_3_out);
  not not_8 (not_8_out, P3);
  and and_4 (and_4_out, not_1_out, P0);
  and and_5 (and_5_out, en, not_2_out);
  and and_6 (and_6_out, not_3_out, P1);
  and and_7 (and_7_out, and_1_out, not_4_out);
  and and_8 (and_8_out, not_5_out, P2);
  and and_9 (and_9_out, and_2_out, not_6_out);
  and and_10 (and_10_out, not_7_out, P3);
  and and_11 (and_11_out, and_3_out, not_8_out);
  or or_1 (or_1_out, and_4_out, and_5_out);
  or or_2 (or_2_out, and_6_out, and_7_out);
  or or_3 (or_3_out, and_8_out, and_9_out);
  or or_4 (or_4_out, and_10_out, and_11_out);
  not not_9 (not_9_out, CLK);
  not not_10 (not_10_out, CLK);
  not not_11 (not_11_out, CLK);
  not not_12 (not_12_out, CLK);
  and and_12 (and_12_out, or_5_out, CLK);
  and and_13 (and_13_out, or_1_out, not_9_out);
  and and_14 (and_14_out, or_6_out, CLK);
  and and_15 (and_15_out, or_2_out, not_10_out);
  and and_16 (and_16_out, or_7_out, CLK);
  and and_17 (and_17_out, or_3_out, not_11_out);
  and and_18 (and_18_out, or_8_out, CLK);
  and and_19 (and_19_out, or_4_out, not_12_out);
  or or_5 (or_5_out, and_12_out, and_13_out);
  or or_6 (or_6_out, and_14_out, and_15_out);
  or or_7 (or_7_out, and_16_out, and_17_out);
  or or_8 (or_8_out, and_18_out, and_19_out);
  Multiplexer multiplexer_1 (.sel(CLK), .in_0(P0), .in_1(or_5_out), .out(P0));
  Multiplexer multiplexer_2 (.sel(CLK), .in_0(P1), .in_1(or_6_out), .out(P1));
  Multiplexer multiplexer_3 (.sel(CLK), .in_0(P2), .in_1(or_7_out), .out(P2));
  Multiplexer multiplexer_4 (.sel(CLK), .in_0(P3), .in_1(or_8_out), .out(P3));
  assign P = P_out ? {4'b0000, P3, P2, P1, P0} : 8'bz;  // Driver driver_1
endmodule
