// Digital circuit RAM_git.dig as structural Verilog
module RAM_git (
  input  CLK,
  input  [3:0] Addr,
  input  RI,
  input  [7:0] A,
  output [7:0] D
);

  wire and_1_out, and_2_out, and_3_out, and_4_out, and_5_out, and_6_out, and_7_out, and_8_out, and_9_out,
       and_10_out, and_11_out, and_12_out, and_13_out, and_14_out, and_15_out, and_16_out, and_17_out,
       and_18_out, and_19_out, and_20_out, and_21_out, and_22_out, and_23_out, and_24_out, and_25_out,
       multiplexer_1_out, multiplexer_7_out, multiplexer_9_out, not_1_out, not_2_out, not_3_out, not_4_out,
       not_5_out, not_6_out, not_7_out, not_8_out, not_9_out, not_10_out, not_11_out, not_12_out, not_13_out,
       not_14_out, not_15_out, or_1_out, or_2_out, or_3_out, or_4_out, or_5_out, or_6_out, or_7_out,
       or_8_out, or_9_out, or_10_out;
  wire [3:0] multiplexer_2_out, multiplexer_6_out;
  wire [7:0] multiplexer_8_out, rom_1_d;

  and and_1 (and_1_out, multiplexer_7_out, multiplexer_1_out);
  and and_2 (and_2_out, multiplexer_7_out, multiplexer_1_out, multiplexer_2_out[0]);
  and and_3 (and_3_out, multiplexer_7_out, multiplexer_1_out, multiplexer_2_out[0], multiplexer_2_out[1]);
  and and_4 (and_4_out, multiplexer_7_out, multiplexer_1_out, multiplexer_2_out[0], multiplexer_2_out[1], multiplexer_2_out[2]);
  not not_1 (not_1_out, multiplexer_7_out);
  not not_2 (not_2_out, multiplexer_1_out);
  not not_3 (not_3_out, and_1_out);
  not not_4 (not_4_out, multiplexer_2_out[0]);
  not not_5 (not_5_out, and_2_out);
  not not_6 (not_6_out, multiplexer_2_out[1]);
  not not_7 (not_7_out, and_3_out);
  not not_8 (not_8_out, multiplexer_2_out[2]);
  not not_9 (not_9_out, and_4_out);
  not not_10 (not_10_out, multiplexer_2_out[3]);
  and and_5 (and_5_out, not_1_out, multiplexer_1_out);
  and and_6 (and_6_out, multiplexer_7_out, not_2_out);
  and and_7 (and_7_out, not_3_out, multiplexer_2_out[0]);
  and and_8 (and_8_out, and_1_out, not_4_out);
  and and_9 (and_9_out, not_5_out, multiplexer_2_out[1]);
  and and_10 (and_10_out, and_2_out, not_6_out);
  and and_11 (and_11_out, not_7_out, multiplexer_2_out[2]);
  and and_12 (and_12_out, and_3_out, not_8_out);
  and and_13 (and_13_out, not_9_out, multiplexer_2_out[3]);
  and and_14 (and_14_out, and_4_out, not_10_out);
  or or_1 (or_1_out, and_5_out, and_6_out);
  or or_2 (or_2_out, and_7_out, and_8_out);
  or or_3 (or_3_out, and_9_out, and_10_out);
  or or_4 (or_4_out, and_11_out, and_12_out);
  or or_5 (or_5_out, and_13_out, and_14_out);
  not not_11 (not_11_out, CLK);
  not not_12 (not_12_out, CLK);
  not not_13 (not_13_out, CLK);
  not not_14 (not_14_out, CLK);
  not not_15 (not_15_out, CLK);
  and and_15 (and_15_out, or_6_out, CLK);
  and and_16 (and_16_out, or_1_out, not_11_out);
  and and_17 (and_17_out, or_7_out, CLK);
  and and_18 (and_18_out, or_2_out, not_12_out);
  and and_19 (and_19_out, or_8_out, CLK);
  and and_20 (and_20_out, or_3_out, not_13_out);
  and and_21 (and_21_out, or_9_out, CLK);
  and and_22 (and_22_out, or_4_out, not_14_out);
  and and_23 (and_23_out, or_10_out, CLK);
  and and_24 (and_24_out, or_5_out, not_15_out);
  or or_6 (or_6_out, and_15_out, and_16_out);
  or or_7 (or_7_out, and_17_out, and_18_out);
  or or_8 (or_8_out, and_19_out, and_20_out);
  or or_9 (or_9_out, and_21_out, and_22_out);
  or or_10 (or_10_out, and_23_out, and_24_out);
  Multiplexer multiplexer_1 (.sel(CLK), .in_0(multiplexer_1_out), .in_1(or_6_out), .out(multiplexer_1_out));
  Multiplexer multiplexer_2 (.sel(CLK), .in_0(multiplexer_2_out[0]), .in_1(or_7_out), .out(multiplexer_2_out[0]));
  Multiplexer multiplexer_3 (.sel(CLK), .in_0(multiplexer_2_out[1]), .in_1(or_8_out), .out(multiplexer_2_out[1]));
  Multiplexer multiplexer_4 (.sel(CLK), .in_0(multiplexer_2_out[2]), .in_1(or_9_out), .out(multiplexer_2_out[2]));
  Multiplexer multiplexer_5 (.sel(CLK), .in_0(multiplexer_2_out[3]), .in_1(or_10_out), .out(multiplexer_2_out[3]));
  and and_25 (and_25_out, multiplexer_1_out, multiplexer_2_out[0], multiplexer_2_out[1], multiplexer_2_out[2], multiplexer_2_out[3]);
  Multiplexer #(.Bits(4)) multiplexer_6 (
    .sel(multiplexer_7_out), .in_0(Addr), .in_1(multiplexer_2_out), .out(multiplexer_6_out));
  ROM #(.AddrBits(4), .Bits(8)) rom_1 (.A(multiplexer_2_out), .sel(1'b1), .D(rom_1_d));
  Multiplexer multiplexer_7 (.sel(and_25_out), .in_0(1'b1), .in_1(1'b0), .out(multiplexer_7_out));
  Multiplexer #(.Bits(8)) multiplexer_8 (.sel(multiplexer_7_out), .in_0(A), .in_1(rom_1_d), .out(multiplexer_8_out));
  Multiplexer multiplexer_9 (.sel(multiplexer_7_out), .in_0(RI), .in_1(1'b1), .out(multiplexer_9_out));
  BlockRAMDualPort #(.AddrBits(4), .Bits(8)) blockramdualport_1 (
    .A(multiplexer_6_out), .Din(multiplexer_8_out), .str(multiplexer_9_out), .C(CLK), .D(D));

  // Notes on the sheet:
  //   CLK: Hz: 2
  //   contents of rom_1 (hex, n*v repeats v):
  //   1f,3e,88,76,53,f0,51,f0,52,f0,4*0,7f,7e
endmodule
