// Digital circuit RegisterB_git.dig as structural Verilog
module RegisterB_git (
  input  [7:0] B,
  input  CLK,
  input  B_in,
  output [7:0] B_2
);

  wire and_1_out, and_2_out, and_3_out, and_4_out, and_5_out, and_6_out, and_7_out, and_8_out, and_9_out,
       and_10_out, and_11_out, and_12_out, and_13_out, and_14_out, and_15_out, and_16_out, and_17_out,
       and_18_out, and_19_out, and_20_out, and_21_out, and_22_out, and_23_out, and_24_out, and_25_out,
       multiplexer_1_out, multiplexer_2_out, multiplexer_3_out, multiplexer_4_out, multiplexer_5_out,
       multiplexer_6_out, multiplexer_7_out, multiplexer_8_out, not_1_out, not_2_out, not_3_out, not_4_out,
       not_5_out, not_6_out, not_7_out, not_8_out, or_1_out, or_2_out, or_3_out, or_4_out, or_5_out,
       or_6_out, or_7_out, or_8_out;

  and and_1 (and_1_out, 1'b0, 1'b0);
  and and_2 (and_2_out, 1'b0, 1'b0);
  and and_3 (and_3_out, 1'b0, 1'b0);
  and and_4 (and_4_out, 1'b0, 1'b0);
  and and_5 (and_5_out, 1'b0, 1'b0);
  and and_6 (and_6_out, 1'b0, 1'b0);
  and and_7 (and_7_out, 1'b0, 1'b0);
  and and_8 (and_8_out, 1'b0, 1'b0);
  not not_1 (not_1_out, 1'b0);
  not not_2 (not_2_out, 1'b0);
  not not_3 (not_3_out, 1'b0);
  not not_4 (not_4_out, 1'b0);
  not not_5 (not_5_out, 1'b0);
  not not_6 (not_6_out, 1'b0);
  not not_7 (not_7_out, 1'b0);
  not not_8 (not_8_out, 1'b0);
  and and_9 (and_9_out, or_1_out, 1'b0);
  and and_10 (and_10_out, and_1_out, not_1_out);
  and and_11 (and_11_out, or_2_out, 1'b0);
  and and_12 (and_12_out, and_2_out, not_2_out);
  and and_13 (and_13_out, or_3_out, 1'b0);
  and and_14 (and_14_out, and_3_out, not_3_out);
  and and_15 (and_15_out, or_4_out, 1'b0);
  and and_16 (and_16_out, and_4_out, not_4_out);
  and and_17 (and_17_out, or_5_out, 1'b0);
  and and_18 (and_18_out, and_5_out, not_5_out);
  and and_19 (and_19_out, or_6_out, 1'b0);
  and and_20 (and_20_out, and_6_out, not_6_out);
  and and_21 (and_21_out, or_7_out, 1'b0);
  and and_22 (and_22_out, and_7_out, not_7_out);
  and and_23 (and_23_out, or_8_out, 1'b0);
  and and_24 (and_24_out, and_8_out, not_8_out);
  or or_1 (or_1_out, and_9_out, and_10_out);
  or or_2 (or_2_out, and_11_out, and_12_out);
  or or_3 (or_3_out, and_13_out, and_14_out);
  or or_4 (or_4_out, and_15_out, and_16_out);
  or or_5 (or_5_out, and_17_out, and_18_out);
  or or_6 (or_6_out, and_19_out, and_20_out);
  or or_7 (or_7_out, and_21_out, and_22_out);
  or or_8 (or_8_out, and_23_out, and_24_out);
  Multiplexer multiplexer_1 (.sel(1'b0), .in_0(multiplexer_1_out), .in_1(or_1_out), .out(multiplexer_1_out));
  Multiplexer multiplexer_2 (.sel(1'b0), .in_0(multiplexer_2_out), .in_1(or_2_out), .out(multiplexer_2_out));
  Multiplexer multiplexer_3 (.sel(1'b0), .in_0(multiplexer_3_out), .in_1(or_3_out), .out(multiplexer_3_out));
  Multiplexer multiplexer_4 (.sel(1'b0), .in_0(multiplexer_4_out), .in_1(or_4_out), .out(multiplexer_4_out));
  Multiplexer multiplexer_5 (.sel(1'b0), .in_0(multiplexer_5_out), .in_1(or_5_out), .out(multiplexer_5_out));
  Multiplexer multiplexer_6 (.sel(1'b0), .in_0(multiplexer_6_out), .in_1(or_6_out), .out(multiplexer_6_out));
  Multiplexer multiplexer_7 (.sel(1'b0), .in_0(multiplexer_7_out), .in_1(or_7_out), .out(multiplexer_7_out));
  Multiplexer multiplexer_8 (.sel(1'b0), .in_0(multiplexer_8_out), .in_1(or_8_out), .out(multiplexer_8_out));
  and and_25 (and_25_out, CLK, B_in);
  D_FF d_ff_1 (.D(B[0]), .C(and_25_out), .Q(B_2[0]));  // open: nQ
  D_FF d_ff_2 (.D(B[1]), .C(and_25_out), .Q(B_2[1]));  // open: nQ
  D_FF d_ff_3 (.D(B[2]), .C(and_25_out), .Q(B_2[2]));  // open: nQ
  D_FF d_ff_4 (.D(B[3]), .C(and_25_out), .Q(B_2[3]));  // open: nQ
  D_FF d_ff_5 (.D(B[4]), .C(and_25_out), .Q(B_2[4]));  // open: nQ
  D_FF d_ff_6 (.D(B[5]), .C(and_25_out), .Q(B_2[5]));  // open: nQ
  D_FF d_ff_7 (.D(B[6]), .C(and_25_out), .Q(B_2[6]));  // open: nQ
  D_FF d_ff_8 (.D(B[7]), .C(and_25_out), .Q(B_2[7]));  // open: nQ
endmodule
