// Digital circuit SAP_git.dig as structural Verilog
module SAP_git (
  input  CLK,
  input  clk_2,
  input  LT,
  input  clk_3,
  output [7:0] Data_BUS,
  output [7:0] A,
  output [7:0] B,
  output [7:0] PC,
  output C,
  output Z,
  output [3:0] OPCODE
);

  wire alu_git_1_c, alu_git_1_z, and_2_out, cc_git_1_p2, control_git_1_p2, control_git_1_p3,
       control_git_1_p4, control_git_1_p5, control_git_1_p6, control_git_1_p7, control_git_1_p8,
       control_git_1_p9, control_git_1_p10, control_git_1_p11, control_git_1_p12, control_git_1_p13,
       control_git_1_p14, control_git_1_p15, control_git_1_p16, multiplexer_5_out, not_1_out;
  wire [2:0] cc_git_1_p5;
  wire [3:0] counter_1_out, ir_git_1_p5, mar_git_1_p4, multiplexer_2_out, multiplexer_3_out;
  wire [7:0] alu_git_1_s, blockramdualport_1_d, multiplexer_1_out, multiplexer_4_out, rom_1_d;

  not not_1 (not_1_out, control_git_1_p2);
  // CC_git cc_git_1: pin names not known; wires that end beside it: 1'b1, cc_git_1_p2, cc_git_1_p5[0], cc_git_1_p5[1], cc_git_1_p5[2]
  and and_1 (cc_git_1_p2, CLK, not_1_out);
  // Control_git control_git_1: pin names not known; wires that end beside it: {Z, C, OPCODE, cc_git_1_p5}, control_git_1_p2, control_git_1_p3, control_git_1_p4, control_git_1_p5, control_git_1_p6, control_git_1_p7, control_git_1_p8, control_git_1_p9, control_git_1_p10, control_git_1_p11, control_git_1_p12, control_git_1_p13, control_git_1_p14, control_git_1_p15, control_git_1_p16
  FLAG_git flag_git_1 (.CLK(cc_git_1_p2), .en(control_git_1_p15), .Z(alu_git_1_z), .C(alu_git_1_c), .Z_2(Z), .C_2(C));
  // RegisterA_git registera_git_1: pin names not known; wires that end beside it: Data_BUS, cc_git_1_p2, control_git_1_p8, A
  PC_git pc_git_1 (.en(control_git_1_p12), .CLK(cc_git_1_p2), .J(control_git_1_p14), .I(Data_BUS), .P(PC));
  and and_2 (and_2_out, control_git_1_p6, control_git_1_p8);
  // IR_git ir_git_1: pin names not known; wires that end beside it: Data_BUS, cc_git_1_p2, control_git_1_p7, cc_git_1_p2, {OPCODE, ir_git_1_p5}
  assign Data_BUS = control_git_1_p13 ? PC : 8'bz;  // Driver driver_1
  assign Data_BUS = control_git_1_p16 ? A : 8'bz;  // Driver driver_2
  RegisterB_git registerb_git_1 (.B(Data_BUS), .CLK(cc_git_1_p2), .B_in(control_git_1_p11), .B_2(B));
  // MAR_git mar_git_1: pin names not known; wires that end beside it: Data_BUS, cc_git_1_p2, control_git_1_p3, mar_git_1_p4
  Multiplexer #(.Bits(8)) multiplexer_1 (.sel(control_git_1_p9), .in_0(B), .in_1({8{1'b0}}), .out(multiplexer_1_out));
  ALU_git alu_git_1 (
    .B(multiplexer_1_out), .A(A), .SUB(control_git_1_p10), .C(alu_git_1_c), .Z(alu_git_1_z), .S(alu_git_1_s));
  Multiplexer #(.Bits(4)) multiplexer_2 (.sel(and_2_out), .in_0(OPCODE), .in_1(4'b0000), .out(multiplexer_2_out));
  assign Data_BUS = control_git_1_p6 ? {multiplexer_2_out, ir_git_1_p5} : 8'bz;  // Driver driver_3
  assign Data_BUS = control_git_1_p9 ? alu_git_1_s : 8'bz;  // Driver driver_4
  ROM #(.AddrBits(4), .Bits(8)) rom_1 (.A(counter_1_out), .sel(1'b1), .D(rom_1_d));
  Multiplexer #(.Bits(4)) multiplexer_3 (.sel(LT), .in_0(mar_git_1_p4), .in_1(counter_1_out), .out(multiplexer_3_out));
  Multiplexer #(.Bits(8)) multiplexer_4 (.sel(LT), .in_0(A), .in_1(rom_1_d), .out(multiplexer_4_out));
  Multiplexer multiplexer_5 (.sel(LT), .in_0(control_git_1_p4), .in_1(1'b1), .out(multiplexer_5_out));
  BlockRAMDualPort #(.AddrBits(4), .Bits(8)) blockramdualport_1 (
    .A(multiplexer_3_out), .Din(multiplexer_4_out), .str(multiplexer_5_out), .C(clk_2),
    .D(blockramdualport_1_d));
  assign Data_BUS = control_git_1_p5 ? blockramdualport_1_d : 8'bz;  // Driver driver_5
  Counter #(.Bits(4)) counter_1 (.en(LT), .C(clk_3), .clr(1'b0), .out(counter_1_out));  // open: ovf

  // Notes on the sheet:
  //   CLK: Hz: 2
  //   clk_2: Hz: 100
  //   clk_3: Hz: 50
  //   contents of rom_1 (hex, n*v repeats v):
  //   1f,3e,88,76,51,f0,53,f0,52,f0,4*0,7f,80
endmodule
